# Fritzing sketch RPi_voltmeter (saved by Fritzing 0.9.3b)

parts:
  IC1 = MCP3008 8-channel 10-bit ADC [part_number=MCP3008]
  Raspberry_Pi_1 = Raspberry Pi 3 [part_number=RPI-3-V1.2]
  R1 = Resistor [tolerance=±5% resistance=220 package="0603 [SMD]"]
  R2 = Resistor [tolerance=±5% resistance=220 package="0603 [SMD]"]
  R3 = Resistor [tolerance=±5% resistance=220 package="0603 [SMD]"]
  R4 = Resistor [tolerance=±5% resistance=220 package="0603 [SMD]"]  # not connected
  R5 = Resistor [tolerance=±5% resistance=220 package="0603 [SMD]"]
  R6 = Resistor [tolerance=±5% resistance=220 package="0603 [SMD]"]  # not connected
  R7 = Resistor [tolerance=±5% resistance=220 package="0603 [SMD]"]  # not connected
  R8 = Resistor [tolerance=±5% resistance=220 package="0603 [SMD]"]
  R9 = Resistor [tolerance=±5% resistance=220 package="0603 [SMD]"]  # not connected
  R10 = Resistor [tolerance=±5% resistance=220 package="0603 [SMD]"]
  R11 = Resistor [tolerance=±5% resistance=220 package="0603 [SMD]"]
  R12 = Resistor [tolerance=±5% resistance=220 package="0603 [SMD]"]
  R13 = Resistor [tolerance=±5% resistance=220 package="0603 [SMD]"]
  R14 = Resistor [tolerance=±5% resistance=220 package="0603 [SMD]"]
  R15 = Resistor [tolerance=±5% resistance=220 package="0603 [SMD]"]
  R16 = Resistor [tolerance=±5% resistance=220 package="0603 [SMD]"]
  R17 = Resistor [tolerance=±5% resistance=220 package="0603 [SMD]"]
  R18 = Resistor [tolerance=±5% resistance=220 package="0603 [SMD]"]
  R19 = Resistor [tolerance=±5% resistance=220 package="0603 [SMD]"]  # not connected
  R20 = Resistor [tolerance=±5% resistance=220 package="0603 [SMD]"]
  R21 = Resistor [tolerance=±5% resistance=220 package="0603 [SMD]"]  # not connected
  R22 = Resistor [tolerance=±5% resistance=220 package="0603 [SMD]"]
  R23 = Resistor [tolerance=±5% resistance=220 package="0603 [SMD]"]
  R24 = Resistor [tolerance=±5% resistance=220 package="0603 [SMD]"]  # not connected
  R25 = Resistor [tolerance=±5% resistance=220 package="0603 [SMD]"]
  R26 = Resistor [tolerance=±5% resistance=220 package="0603 [SMD]"]  # not connected
  Part1 = INA219 High Side DC Current Sensor Breakout [part_number=904]
  R27 = Resistor [tolerance=±5% resistance=220 package="2010 [SMD]"]
  R28 = Resistor [tolerance=±5% resistance=220 package="2010 [SMD]"]  # not connected
  R29 = Resistor [tolerance=±5% resistance=220 package="2010 [SMD]"]
  R30 = Resistor [tolerance=±5% resistance=220 package="2010 [SMD]"]  # not connected

nets:
  N1: IC1.no_name_yet#1, R2.Pin_0
  N2: IC1.no_name_yet#2, R5.Pin_0
  N3: IC1.no_name_yet#3, R8.Pin_0
  N4: IC1.no_name_yet#4, R11.Pin_0
  N5: IC1.no_name_yet#10, Raspberry_Pi_1.GPIO8
  N6: IC1.no_name_yet#11, Raspberry_Pi_1.GPIO10
  N7: IC1.no_name_yet#12, Raspberry_Pi_1.GPIO9
  N8: IC1.no_name_yet#13, Raspberry_Pi_1.GPIO11
  N9: IC1.no_name_yet#14, Raspberry_Pi_1.GND
  N10: IC1.no_name_yet#16, Raspberry_Pi_1.3v3
  N11: Raspberry_Pi_1.GPIO2, Part1.SDA
  N12: Raspberry_Pi_1.GPIO3, Part1.SCL
  N13: R1.Pin_0, R10.Pin_0
  N14: R3.Pin_0, R12.Pin_0
  N15: R13.Pin_0, R16.Pin_1
  N16: R14.Pin_0, R18.Pin_1
  N17: R15.Pin_0, R20.Pin_1
  N18: R17.Pin_1, R23.Pin_1
  N19: R22.Pin_1, R25.Pin_0
  N20: Part1.VIN-, R27.Pin_1
  N21: Part1.VIN+, R29.Pin_1

notes:
  Voltage Sensor 1
  GND +
  OUT -
  V
  Voltage Sensor 2
  GND +
  OUT -
  V
  Voltage Sensor 3
  GND +
  OUT -
  V
  Voltage Sensor 4
  GND +
  OUT -
  V
  Circuit
  V1
  V2
  V3
  GND
  Buck Converter
  V
  GND
  + -
  Load
  Circuit +
  -
  Current sensor is connected in series with load

custom parts:
  INA219 High Side DC Current Sensor Breakout: This breakout board will solve all your power-monitoring problems. Instead of struggling with two multimeters, you can just use the handy INA219B chip on this breakout to both measure both the high side voltage and DC current draw over I2C with 1% precision. Most current-measuring devices such as our current panel meter are only good for low side measuring. That means that unless you want to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
